# Fritzing sketch Schaltbild (saved by Fritzing 0.9.3b)
breadboards: 2

parts:
  Bauteil1 = Arduino Nano (Rev3.0)
  U1 = I2C Extender [package=dip]
  VCC1 = 4 x AAA Battery Mount
  U4 = I2C Extender [package=dip]
  Teraranger_Evo_60_m1 = Teraranger Evo 60M Connector [part_number=DF13#-4P-1.25V package=DF13C-4P-1.25V]
  U5 = SWITCH_SPDT [package=kps-1290]
  microSD1 = MicroSD Card Module
  DFRobot_DFPlayer_Mini1 = DFRobot DFPlayer Mini [part_number=DFR0299]
  U6 = LCD-16X2 [package=lcd-16x2_nosilk]
  LCM1602_IIC1 = LCM1602 IIC [part_number="LCM1602 IIC" chip_label="LCM1602 IIC" package="DIP (Dual Inline) [THT]"]
  R4 = Resistor [tolerance=±5% resistance=1k package=THT]
  Klinkenkabel = Audio Jack (TRRS) 3.5mm [part_number="LUMBERG JEITA RC-5325A" package="RC-5325A [SMD]"]
  LED2 = smd LED [color="Green (555nm)" package="1206 [SMD]"]
  R5 = Resistor [tolerance=±5% resistance=150 package=THT]
  R7 = Resistor [tolerance=±5% resistance=1.5k package="0805 [SMD]"]
  R8 = Resistor [tolerance=±5% resistance=1.5k package="0805 [SMD]"]
  R9 = Resistor [tolerance=±5% resistance=100 package=THT]
  R10 = Resistor [tolerance=±5% resistance=100 package=THT]
  S2 = Momentary Switch [package=ksa_sealed_tac_switch]

nets:
  GND: Bauteil1.GND, U1.GND, VCC1.-, U4.GND, Teraranger_Evo_60_m1.3, microSD1.GND, DFRobot_DFPlayer_Mini1.GND-1, DFRobot_DFPlayer_Mini1.GND-2, LCM1602_IIC1.GND, Klinkenkabel.RING2, LED2.cathode, S2.3, S2.4
  N1: Bauteil1.D2, S2.1, S2.2
  N2: Bauteil1.D5, DFRobot_DFPlayer_Mini1.TX
  N3: Bauteil1.D6, R4.Pin_0
  N4: Bauteil1.D10, microSD1.CS
  N5: Bauteil1.D11/MOSI, microSD1.MOSI
  N6: Bauteil1.D12/MISO, microSD1.MISO
  VCC: Bauteil1.VIN, U1.VCC, U4.VCC, Teraranger_Evo_60_m1.7, U5.P, microSD1.VCC, DFRobot_DFPlayer_Mini1.VCC, LCM1602_IIC1.VCC, R5.Pin_1, R7.Pin_1, R8.Pin_1
  N7: Bauteil1.A5, U1.Sy, LCM1602_IIC1.SCL
  N8: Bauteil1.A4, U1.Sx, LCM1602_IIC1.SDA
  N9: Bauteil1.D13/SCK, microSD1.SCK
  N10: U1.Lx, U4.Lx, R8.Pin_0
  N11: U1.Ly, U4.Ly, R7.Pin_0
  N12: VCC1.+, U5.O
  N13: U4.Sx, Teraranger_Evo_60_m1.4
  N14: U4.Sy, Teraranger_Evo_60_m1.5
  N15: DFRobot_DFPlayer_Mini1.RX, R4.Pin_1
  N16: DFRobot_DFPlayer_Mini1.DAC_R, R9.Pin_1
  N17: DFRobot_DFPlayer_Mini1.DAC_L, R10.Pin_1
  VSS: U6.VSS, LCM1602_IIC1.VSS
  VDD: U6.VDD, LCM1602_IIC1.VDD
  N18: U6.VO, LCM1602_IIC1.V0
  N19: U6.RS, LCM1602_IIC1.RS
  N20: U6.R_W, LCM1602_IIC1.RW
  N21: U6.E, LCM1602_IIC1.E
  N22: U6.DB0, LCM1602_IIC1.D0
  N23: U6.DB1, LCM1602_IIC1.D1
  N24: U6.DB2, LCM1602_IIC1.D2
  N25: U6.DB3, LCM1602_IIC1.D3
  N26: U6.DB4, LCM1602_IIC1.D4
  N27: U6.DB5, LCM1602_IIC1.D5
  N28: U6.DB6, LCM1602_IIC1.D6
  N29: U6.DB7, LCM1602_IIC1.D7
  N30: U6.A, LCM1602_IIC1.A
  N31: U6.K, LCM1602_IIC1.K
  N32: LCM1602_IIC1.LED_A, LCM1602_IIC1.LED_B
  N33: Klinkenkabel.TIP, R10.Pin_0
  N34: Klinkenkabel.RING1, R9.Pin_0
  N35: LED2.anode, R5.Pin_0

custom parts:
  Teraranger Evo 60M Connector: Teraranger Evo 60M Connector - reduziert auf genutzte Pins
  LCM1602 IIC: I2C-Module to use a 1602 or 2004 LCD on with the wire.h libory Serial LCD Modul
